// Logisim project podium.circ as structural Verilog: 1 circuit, main circuit main
module main (
  input  in_1,
  input  in_2,
  input  in_3,
  output out_4,
  output out_5,
  output out_6
);

  wire and_2_out, not_1_out, not_2_out;

  buf and_1 (in_3, in_1);  // AND_Gate
  and and_2 (and_2_out, in_2, in_3);
  and and_3 (out_4, in_3, and_2_out);
  not not_1 (not_1_out, and_2_out);
  not not_2 (not_2_out, in_3);
  and and_4 (out_5, in_3, not_1_out);
  and and_5 (out_6, not_2_out, and_2_out);
endmodule
